# Fritzing sketch Schema ventola (saved by Fritzing 0.9.3b)
breadboards: 1

parts:
  Raspberry_Pi_1 = Raspberry Pi 3 [part_number=RPI-3-V1.2]
  X1 = USB Connectors [package=usb-a-pcb]
  Componente1 = BME280 Breakout
  KY-1 = Keyes Relay [package=THT]
  LED1 = LED - 5mm [color="Red (633nm)" package="5 mm [THT]"]
  LED2 = LED - 5mm [color="Green (555nm)" package="5 mm [THT]"]
  R1 = Resistor [tolerance=±5% resistance=220 package="0805 [SMD]"]
  R2 = Resistor [tolerance=±5% resistance=220 package="0805 [SMD]"]

nets:
  3V3: Raspberry_Pi_1.3v3, Raspberry_Pi_1.3V3, Componente1.3.3V
  N1: Raspberry_Pi_1.GPIO2, Componente1.SDI/SDA
  N2: Raspberry_Pi_1.GPIO3, Componente1.SCK/SCL
  N3: Raspberry_Pi_1.GIPO4, KY-1.signal
  GND: Raspberry_Pi_1.GND, Componente1.GND, KY-1.ground, KY-1.C
  N4: Raspberry_Pi_1.5V, X1.VBUS, KY-1.power, R2.Pin_1
  N5: X1.GND, KY-1.NO, LED2.anode
  N6: KY-1.NC, LED1.anode
  N7: LED1.cathode, R1.Pin_0
  N8: LED2.cathode, R2.Pin_0

notes:
  To USB Fan
  Other USB connections are not needed
  BME280 Sensor
  Wire colors:
  Red → +5V
  White → +3.3V
  Black → GND
  Brown → NC GND
  Cyan → SDA
  Yellow → SCL
  Green → Signal
  Relay connections:
  NC → Normally closed (triggers red LED)
  COM → Common interface (GND from RPi)
  NO → Normally Open (triggers green LED and USB fan)

custom parts:
  Keyes Relay: The Keyes 5V relay module is suitable for SCM development, home appliance control. It uses a 5V~12V TIL control signal which can control DC / AC signal.
